# Fritzing sketch flow_sensor (saved by Fritzing 0.8.7b)

parts:
  JACK1 = 2.1mm Barrel Jack with Terminal Block
  U2 = LM2596 step down module [part_number="12V --> 5V"]
  U4 = ESP8266 NodeMCU LoLin module
  YF-S201_Flow_Meter1 = YF-S201 Water Flow Meter

nets:
  N1: JACK1.POS, U2.IN+, U4.Vin
  GND: JACK1.NEG, U2.IN-, U2.OUT-, U4.GND, YF-S201_Flow_Meter1.GND
  N2: U2.OUT+, YF-S201_Flow_Meter1.VCC
  N3: U4.D0, YF-S201_Flow_Meter1.SIG

notes:
  Power Supply 12V

custom parts:
  LM2596 step down module: LM2596 DC-DC step down power supply module 3 A.
  ESP8266 NodeMCU LoLin module: ESP8266 based NodeMCU
  YF-S201 Water Flow Meter: The YF-S201 Flow Meter. The input voltage is 5V to 24V (DC).
