# Fritzing sketch photocells (saved by Fritzing 0.8.7b)

parts:
  R1 = PHOTOCELL [package=photocell-kit]
  R5 = Resistor [tolerance=±5% resistance=1k package="1206 [SMD]"]
  JACK1 = 2.1mm Barrel Jack with Terminal Block
  U2 = LM2596 step down module [part_number="12V --> 5V"]
  SparkFun_74HC4051_8-Channel_Mux_Breakout1 = SparkFun-74HC4051-8-Channel-Mux-Breakout [part_number=BOB-13906]
  U4 = ESP8266 NodeMCU LoLin module
  R10 = PHOTOCELL [package=photocell-kit]
  R11 = Resistor [tolerance=±5% resistance=1k package="1206 [SMD]"]

nets:
  N1: R1.P$1, R5.Pin_0, SparkFun_74HC4051_8-Channel_Mux_Breakout1.Y2
  N2: R1.P$2, U2.OUT+, SparkFun_74HC4051_8-Channel_Mux_Breakout1.VCC, R10.P$2
  GND: R5.Pin_1, JACK1.NEG, U2.IN-, U2.OUT-, SparkFun_74HC4051_8-Channel_Mux_Breakout1.GND, U4.GND, R11.Pin_1
  N3: JACK1.POS, U2.IN+, U4.Vin
  N4: SparkFun_74HC4051_8-Channel_Mux_Breakout1.Y3, R10.P$1, R11.Pin_0
  N5: SparkFun_74HC4051_8-Channel_Mux_Breakout1.S2, U4.D7
  N6: SparkFun_74HC4051_8-Channel_Mux_Breakout1.S1, U4.D6
  N7: SparkFun_74HC4051_8-Channel_Mux_Breakout1.S0, U4.D5
  N8: SparkFun_74HC4051_8-Channel_Mux_Breakout1.Z, U4.A0

notes:
  Power Supply 12V

custom parts:
  LM2596 step down module: LM2596 DC-DC step down power supply module 3 A.
  ESP8266 NodeMCU LoLin module: ESP8266 based NodeMCU
