# Fritzing sketch dht11 (saved by Fritzing 0.8.7b)

parts:
  DHT1 = DHT11 Humitidy and Temperature Sensor
  R3 = Resistor [tolerance=±5% resistance=10k package="1206 [SMD]"]
  JACK1 = 2.1mm Barrel Jack with Terminal Block
  U2 = LM2596 step down module [part_number="12V --> 5V"]
  U4 = ESP8266 NodeMCU LoLin module

nets:
  N1: DHT1.VDD, R3.Pin_1, U2.OUT+
  N2: DHT1.DATA, R3.Pin_0, U4.D1
  GND: DHT1.GND, JACK1.NEG, U2.IN-, U2.OUT-, U4.GND
  N3: JACK1.POS, U2.IN+, U4.Vin

notes:
  Power Supply 12V

custom parts:
  DHT11 Humitidy and Temperature Sensor: DHT11 Humidity and Temperature Sensor
  LM2596 step down module: LM2596 DC-DC step down power supply module 3 A.
  ESP8266 NodeMCU LoLin module: ESP8266 based NodeMCU
