# Fritzing sketch flow_sensor (saved by Fritzing 0.8.7b)

parts:
  YF-S201_Flow_Meter2 = YF-S201 Water Flow Meter
  JACK2 = 2.1mm Barrel Jack with Terminal Block
  U7 = ESP32-38PinWide [part_number=ESP32-38PinWide]
  U8 = LM2596 step down module

nets:
  N1: YF-S201_Flow_Meter2.SIG, U7.GPIO39
  GND: YF-S201_Flow_Meter2.GND, JACK2.NEG, U7.GND, U8.IN-, U8.OUT-
  VCC: YF-S201_Flow_Meter2.VCC, U7.VIN, U8.OUT+
  N2: JACK2.POS, U8.IN+

notes:
  Power Supply 12V

custom parts:
  YF-S201 Water Flow Meter: The YF-S201 Flow Meter. The input voltage is 5V to 24V (DC).
  ESP32-38PinWide: Generic 38-Pin ESP32 with wide format (only access to one side of pins on a breadboard) based on Stephen Lilley's HiLetgo ESP-WROOM-32 ESP32 ESP-32S Development Board.
  LM2596 step down module: LM2596 DC-DC step down power supply module 3 A.
