# Fritzing sketch moisture_sensors (saved by Fritzing 0.8.7b)

parts:
  Capacitive_Soil_Moisture_Sensor3 = DFRobot Capacitive Soil Moisture Sensor V1.0 [part_number=SEN0193]
  Capacitive_Soil_Moisture_Sensor4 = DFRobot Capacitive Soil Moisture Sensor V1.0 [part_number=SEN0193]
  JACK2 = 2.1mm Barrel Jack with Terminal Block
  U7 = ESP32-38PinWide [part_number=ESP32-38PinWide]
  U8 = LM2596 step down module

nets:
  N1: Capacitive_Soil_Moisture_Sensor3.A, U7.GPIO35
  VCC: Capacitive_Soil_Moisture_Sensor3.VCC, Capacitive_Soil_Moisture_Sensor4.VCC, U7.VIN, U8.OUT+
  GND: Capacitive_Soil_Moisture_Sensor3.GND, Capacitive_Soil_Moisture_Sensor4.GND, JACK2.NEG, U7.GND, U8.IN-, U8.OUT-
  N2: Capacitive_Soil_Moisture_Sensor4.A, U7.GPIO32
  N3: JACK2.POS, U8.IN+

notes:
  Power Supply 12V

custom parts:
  DFRobot Capacitive Soil Moisture Sensor V1.0: DFRobot Capacitive Soil Moisture Sensor V1.0 This product measures soil moisture levels by capacitive sensing, rather than resistive sensing like other types of moisture sensor. It is made of a corrosion resistant material giving it a long service life. Insert it into soil and impress your friends with the real-time soil moisture data! The product includes an on-board voltage regulator which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
  ESP32-38PinWide: Generic 38-Pin ESP32 with wide format (only access to one side of pins on a breadboard) based on Stephen Lilley's HiLetgo ESP-WROOM-32 ESP32 ESP-32S Development Board.
  LM2596 step down module: LM2596 DC-DC step down power supply module 3 A.
