# Fritzing sketch photocell (saved by Fritzing 0.8.7b)

parts:
  R13 = Resistor [tolerance=±5% resistance=1k package="1206 [SMD]"]
  JACK2 = 2.1mm Barrel Jack with Terminal Block
  R16 = PHOTOCELL [package=photocell-kit]
  U7 = ESP32-38PinWide [part_number=ESP32-38PinWide]
  U8 = LM2596 step down module

nets:
  N1: R13.Pin_0, R16.P$2, U7.GPIO34
  N2: R13.Pin_1, JACK2.NEG, U7.GND, U8.IN-, U8.OUT-
  N3: JACK2.POS, U8.IN+
  N4: R16.P$1, U7.VIN, U8.OUT+

notes:
  Power Supply 12V

custom parts:
  ESP32-38PinWide: Generic 38-Pin ESP32 with wide format (only access to one side of pins on a breadboard) based on Stephen Lilley's HiLetgo ESP-WROOM-32 ESP32 ESP-32S Development Board.
  LM2596 step down module: LM2596 DC-DC step down power supply module 3 A.
