# Fritzing sketch solenoid_valve (saved by Fritzing 0.8.7b)

parts:
  VALVE2 = Plastic Solenoid Valve
  D2 = Diode [package=diode-1n4001]
  R12 = Resistor [tolerance=±5% resistance=10k package="1206 [SMD]"]
  JACK2 = 2.1mm Barrel Jack with Terminal Block
  FET2 = STP16NF06 N-Channel Power MOSFET
  U7 = ESP32-38PinWide [part_number=ESP32-38PinWide]
  U8 = LM2596 step down module

nets:
  N1: VALVE2.no_name_yet#1, D2.A, JACK2.POS, U8.IN+
  N2: VALVE2.no_name_yet#2, D2.C, FET2.source
  N3: R12.Pin_0, U7.GPIO33
  N4: R12.Pin_1, FET2.gate
  N5: JACK2.NEG, FET2.drain, U7.GND, U8.IN-, U8.OUT-
  N6: U7.VIN, U8.OUT+

notes:
  Power Supply 12V

custom parts:
  STP16NF06 N-Channel Power MOSFET: STP16NF06 N-channel Power MOSFET
  ESP32-38PinWide: Generic 38-Pin ESP32 with wide format (only access to one side of pins on a breadboard) based on Stephen Lilley's HiLetgo ESP-WROOM-32 ESP32 ESP-32S Development Board.
  LM2596 step down module: LM2596 DC-DC step down power supply module 3 A.
